// Logisim project 4BitMagnitudeAddar.circ as structural Verilog: 2 circuits, main circuit main
module main (
  input  A,
  input  B0,
  input  B1,
  input  B2,
  input  B3,
  output S0,
  output S1,
  output S2,
  output S4,
  output C
);

  wire halfaddar_1_c, halfaddar_2_c, halfaddar_3_c;

  halfAddar halfaddar_1 (.A(A), .B(B0), .S(S0), .C(halfaddar_1_c));
  halfAddar halfaddar_2 (.A(halfaddar_1_c), .B(B1), .S(S1), .C(halfaddar_2_c));
  halfAddar halfaddar_3 (.A(halfaddar_2_c), .B(B2), .S(S2), .C(halfaddar_3_c));
  halfAddar halfaddar_4 (.A(halfaddar_3_c), .B(B3), .S(S4), .C(C));
endmodule

module halfAddar (
  input  A,
  input  B,
  output S,
  output C
);

  xor xor_1 (S, A, B);
  and and_1 (C, A, B);
endmodule
