// Logisim project 4bitAddar.circ as structural Verilog: 2 circuits, main circuit main
module main (
  input  A0,
  input  B0,
  input  A1,
  input  B1,
  input  A2,
  input  B2,
  input  A3,
  input  B3,
  output S0,
  output S1,
  output S2,
  output S3,
  output Carry
);

  wire and_1_out, fulladdar_1_cout, fulladdar_2_cout;

  xor xor_1 (S0, A0, B0);
  and and_1 (and_1_out, A0, B0);
  fullAddar fulladdar_1 (.A(A1), .B(B1), .Cin(and_1_out), .Sum(S1), .Cout(fulladdar_1_cout));
  fullAddar fulladdar_2 (.A(A2), .B(B2), .Cin(fulladdar_1_cout), .Sum(S2), .Cout(fulladdar_2_cout));
  fullAddar fulladdar_3 (.A(A3), .B(B3), .Cin(fulladdar_2_cout), .Sum(S3), .Cout(Carry));
endmodule

module fullAddar (
  input  A,
  input  B,
  input  Cin,
  output Sum,
  output Cout
);

  wire and_1_out, and_2_out, xor_1_out;

  xor xor_1 (xor_1_out, A, B);
  and and_1 (and_1_out, A, B);
  xor xor_2 (Sum, xor_1_out, Cin);
  and and_2 (and_2_out, xor_1_out, Cin);
  or or_1 (Cout, and_2_out, and_1_out);
endmodule
