// Logisim project 8to1Multiplexer.circ as structural Verilog: 1 circuit, main circuit main
module main (
  input  S0,
  input  S1,
  input  S2,
  input  I0,
  input  I1,
  input  I2,
  input  I3,
  input  I4,
  input  I5,
  input  I6,
  input  I7,
  output out_12
);

  wire multiplexer_1_out, multiplexer_2_out, multiplexer_3_out, multiplexer_4_out, multiplexer_5_out,
       multiplexer_6_out;

  Multiplexer #(.enable("false")) multiplexer_1 (.in0(I0), .in1(I1), .out(multiplexer_1_out), .sel(S0));
  Multiplexer #(.enable("false")) multiplexer_2 (.in0(I2), .in1(I3), .out(multiplexer_2_out), .sel(S0));
  Multiplexer #(.enable("false")) multiplexer_3 (.in0(I4), .in1(I5), .out(multiplexer_3_out), .sel(S0));
  Multiplexer #(.enable("false")) multiplexer_4 (.in0(I6), .in1(I7), .out(multiplexer_4_out), .sel(S0));
  Multiplexer #(.enable("false")) multiplexer_5 (
    .in0(multiplexer_1_out), .in1(multiplexer_2_out), .out(multiplexer_5_out), .sel(S1));
  Multiplexer #(.enable("false")) multiplexer_6 (
    .in0(multiplexer_3_out), .in1(multiplexer_4_out), .out(multiplexer_6_out), .sel(S1));
  Multiplexer #(.enable("false")) multiplexer_7 (
    .in0(multiplexer_5_out), .in1(multiplexer_6_out), .out(out_12), .sel(S2));
endmodule
