// Logisim project AssignOneQuestion4.circ as structural Verilog: 2 circuits, main circuit a
module a (
  input  A,
  input  B,
  input  C,
  input  D,
  output out_5
);

  wire A_prime_out, AB_out, ACD_out, B_prime_out, BC_prime_out, C_prime_out, D_prime_out, nor_1_out;

  nor A_prime (A_prime_out, A, A);
  nor B_prime (B_prime_out, B, B);
  nor C_prime (C_prime_out, C, C);
  nor D_prime (D_prime_out, D, D);
  nor AB (AB_out, A_prime_out, B_prime_out);
  nor BC_prime (BC_prime_out, B_prime_out, C);
  nor ACD (ACD_out, A_prime_out, C_prime_out, D_prime_out);
  nor nor_1 (nor_1_out, AB_out, BC_prime_out, ACD_out);
  nor nor_2 (out_5, nor_1_out, nor_1_out);

  // Notes on the sheet:
  //   B'C'+B'D'+A'C
  //   A(B+CD)+BC'
endmodule

module b (
  input  A,
  input  B,
  input  C,
  input  D,
  input  E,
  output out_6
);

  wire A_B_prime_out, A_prime_out, C_prime_D_prime_out, CD_E_prime_out, nand_1_out;

  nand A_prime (A_prime_out, A, A);
  nand C_prime_D_prime (C_prime_D_prime_out, C, D);
  nand A_B_prime (A_B_prime_out, A_prime_out, B);
  nand CD_E_prime (CD_E_prime_out, C_prime_D_prime_out, E);
  nand nand_1 (nand_1_out, A_B_prime_out, CD_E_prime_out);
  nand nand_2 (out_6, nand_1_out, nand_1_out);

  // Notes on the sheet:
  //   A'B+EC'+ED'
  //   (A+B')(CD+E')
endmodule
