// Logisim project AssignQuestion5.circ as structural Verilog: 6 circuits, main circuit binaryToGCD
module binaryToGCD (
  input  A,
  input  B,
  input  C,
  input  D,
  output W,
  output X,
  output Y,
  output Z
);

  xor xor_1 (X, A, B);
  xor xor_2 (Y, B, C);
  xor xor_3 (Z, C, D);

  assign W = A;
endmodule

module GCDtobinary (
  input  A,
  input  B,
  input  C,
  input  D,
  output W,
  output X,
  output Y,
  output Z
);

  xor xor_1 (X, A, B);
  xor xor_2 (Y, X, C);
  xor xor_3 (Z, Y, D);

  assign W = A;
endmodule

module BCDtoGCD (
  input  A,
  input  B,
  input  C,
  input  D,
  output W,
  output X,
  output Y,
  output Z
);

  or or_1 (X, A, B);
  xor xor_1 (Y, B, C);
  xor xor_2 (Z, C, D);

  assign W = A;
endmodule

module GCDtoBCD (
  input  A,
  input  B,
  input  C,
  input  D,
  output W,
  output X,
  output Y,
  output Z
);

  wire and_2_out, and_3_out, and_4_out, and_5_out, not_1_out, not_2_out, not_3_out, not_4_out, or_2_out,
       or_3_out, xnor_1_out;

  not not_1 (not_1_out, A);
  not not_2 (not_2_out, B);
  not not_3 (not_3_out, C);
  not not_4 (not_4_out, D);
  and and_1 (X, not_1_out, B);
  and and_2 (and_2_out, not_1_out, B, not_3_out);
  and and_3 (and_3_out, not_2_out, C);
  xnor xnor_1 (xnor_1_out, B, C);
  or or_1 (Y, and_2_out, and_3_out);
  or or_2 (or_2_out, and_2_out, and_3_out);
  or or_3 (or_3_out, A, xnor_1_out);
  and and_4 (and_4_out, or_2_out, not_4_out);
  and and_5 (and_5_out, D, or_3_out);
  or or_4 (Z, and_4_out, and_5_out);

  assign W = A;
endmodule

module BCDtoEx3 (
  input  A,
  input  B,
  input  C,
  input  D,
  output W,
  output X,
  output Y,
  output Z
);

  wire and_1_out, and_2_out, and_3_out, and_4_out, and_5_out, not_1_out, not_2_out;

  not not_1 (not_1_out, B);
  not not_2 (not_2_out, C);
  not not_3 (Z, D);
  and and_1 (and_1_out, B, D);
  and and_2 (and_2_out, B, C);
  and and_3 (and_3_out, C, not_1_out);
  and and_4 (and_4_out, not_1_out, D);
  and and_5 (and_5_out, B, not_2_out, Z);
  xnor xnor_1 (Y, C, D);
  or or_1 (W, A, and_1_out, and_2_out);
  or or_2 (X, and_3_out, and_4_out, and_5_out);
endmodule

module Ex3toBCD (
  input  A,
  input  B,
  input  C,
  input  D,
  output W,
  output X,
  output Y,
  output Z
);

  wire and_1_out, and_2_out, and_4_out, and_5_out, not_1_out, not_2_out, or_1_out;

  not not_1 (not_1_out, B);
  not not_2 (not_2_out, C);
  not not_3 (Z, D);
  or or_1 (or_1_out, B, and_1_out);
  and and_1 (and_1_out, C, D);
  and and_2 (and_2_out, not_1_out, not_2_out);
  and and_3 (W, A, or_1_out);
  and and_4 (and_4_out, and_1_out, B);
  and and_5 (and_5_out, not_1_out, Z);
  xor xor_1 (Y, C, D);
  or or_2 (X, and_2_out, and_4_out, and_5_out);
endmodule
