// Logisim project AssignQuestion6.circ as structural Verilog: 2 circuits, main circuit Q6b
module Q6b (
  input  Cin,
  input  A0,
  input  B0,
  input  A1,
  input  B1,
  input  A2,
  input  B2,
  input  A3,
  input  B3,
  output S0,
  output S1,
  output S2,
  output S3,
  output Cout
);

  wire q6afulladdar_1_cout, q6afulladdar_2_cout, q6afulladdar_3_cout;

  Q6aFullAddar q6afulladdar_1 (.Cin(Cin), .A(A0), .B(B0), .S(S0), .Cout(q6afulladdar_1_cout));
  Q6aFullAddar q6afulladdar_2 (.Cin(q6afulladdar_1_cout), .A(A1), .B(B1), .S(S1), .Cout(q6afulladdar_2_cout));
  Q6aFullAddar q6afulladdar_3 (.Cin(q6afulladdar_2_cout), .A(A2), .B(B2), .S(S2), .Cout(q6afulladdar_3_cout));
  Q6aFullAddar q6afulladdar_4 (.Cin(q6afulladdar_3_cout), .A(A3), .B(B3), .S(S3), .Cout(Cout));
endmodule

module Q6aFullAddar (
  input  Cin,
  input  A,
  input  B,
  output S,
  output Cout
);

  wire and_1_out, and_2_out, and_3_out;

  xor xor_1 (S, Cin, A, B);
  and and_1 (and_1_out, Cin, A);
  and and_2 (and_2_out, A, B);
  and and_3 (and_3_out, B, Cin);
  or or_1 (Cout, and_1_out, and_2_out, and_3_out);
endmodule
