// Logisim project Nand.circ as structural Verilog: 6 circuits, main circuit not
module \not  (
  input  A,
  output out_2
);

  nand nand_1 (out_2, A, A);
endmodule

module \xor  (
  input  A,
  input  B,
  output out_3
);

  wire A_prime_AB_out, A_prime_B_prime_out, B_prime_AB_out;

  nand A_prime_B_prime (A_prime_B_prime_out, A, B);
  nand A_prime_AB (A_prime_AB_out, A, A_prime_B_prime_out);
  nand B_prime_AB (B_prime_AB_out, A_prime_B_prime_out, B);
  nand A_prime_B_AB_prime (out_3, A_prime_AB_out, B_prime_AB_out);
endmodule

module \xnor  (
  input  A,
  input  B,
  output out_3
);

  wire A_prime_AB_out, A_prime_B_AB_prime_out, A_prime_B_prime_out, B_prime_AB_out;

  nand A_prime_B_prime (A_prime_B_prime_out, A, B);
  nand A_prime_AB (A_prime_AB_out, A, A_prime_B_prime_out);
  nand B_prime_AB (B_prime_AB_out, A_prime_B_prime_out, B);
  nand A_prime_B_AB_prime (A_prime_B_AB_prime_out, A_prime_AB_out, B_prime_AB_out);
  nand A_prime_B_prime_AB (out_3, A_prime_B_AB_prime_out, A_prime_B_AB_prime_out);
endmodule

module And (
  input  A,
  input  B,
  output out_3
);

  wire A_prime_B_prime_out;

  nand A_prime_B_prime (A_prime_B_prime_out, A, B);
  nand AB (out_3, A_prime_B_prime_out, A_prime_B_prime_out);
endmodule

module Or (
  input  A,
  input  B,
  output out_3
);

  wire A_prime_out, B_prime_out;

  nand A_prime (A_prime_out, A, A);
  nand B_prime (B_prime_out, B, B, B);
  nand A_B (out_3, A_prime_out, B_prime_out);
endmodule

module Nor (
  input  A,
  input  B,
  output out_3
);

  wire A_B_out, A_prime_out, B_prime_out;

  nand A_prime (A_prime_out, A, A);
  nand B_prime (B_prime_out, B, B, B);
  nand A_B (A_B_out, A_prime_out, B_prime_out);
  nand A_prime_B_prime (out_3, A_B_out, A_B_out);
endmodule
