// Logisim project Nor.circ as structural Verilog: 6 circuits, main circuit not
module \not  (
  input  A,
  output out_2
);

  nor nor_1 (out_2, A, A);
endmodule

module \or  (
  input  A,
  input  B,
  output out_3
);

  wire A_prime_B_prime_out;

  nor A_prime_B_prime (A_prime_B_prime_out, A, B);
  nor A_B (out_3, A_prime_B_prime_out, A_prime_B_prime_out);
endmodule

module \and  (
  input  A,
  input  B,
  output out_3
);

  wire A_prime_out, B_prime_out;

  nor A_prime (A_prime_out, A, A);
  nor B_prime (B_prime_out, B, B);
  nor AB (out_3, A_prime_out, B_prime_out);
endmodule

module \xor  (
  input  A,
  input  B,
  output out_3
);

  wire A_prime_B_out, A_prime_B_prime_AB_out, A_prime_B_prime_out, AB_prime_out;

  nor A_prime_B_prime (A_prime_B_prime_out, A, B);
  nor A_prime_B (A_prime_B_out, A, A_prime_B_prime_out);
  nor AB_prime (AB_prime_out, A_prime_B_prime_out, B);
  nor A_prime_B_prime_AB (A_prime_B_prime_AB_out, A_prime_B_out, AB_prime_out);
  nor A_prime_B_AB_prime (out_3, A_prime_B_prime_AB_out, A_prime_B_prime_AB_out);
endmodule

module \xnor  (
  input  A,
  input  B,
  output out_3
);

  wire A_prime_B_out, A_prime_B_prime_out, AB_prime_out;

  nor A_prime_B_prime (A_prime_B_prime_out, A, B);
  nor A_prime_B (A_prime_B_out, A, A_prime_B_prime_out);
  nor AB_prime (AB_prime_out, A_prime_B_prime_out, B);
  nor A_prime_B_prime_AB (out_3, A_prime_B_out, AB_prime_out);
endmodule

module \nand  (
  input  A,
  input  B,
  output out_3
);

  wire A_prime_out, AB_out, B_prime_out;

  nor A_prime (A_prime_out, A, A);
  nor B_prime (B_prime_out, B, B);
  nor AB (AB_out, A_prime_out, B_prime_out);
  nor A_prime_B_prime (out_3, AB_out, AB_out);
endmodule
