// Logisim project subtractor.circ as structural Verilog: 2 circuits, main circuit halfSubtractor
module halfSubtractor (
  input  A,
  input  B,
  output D,
  output C
);

  wire not_1_out;

  not not_1 (not_1_out, A);
  xor xor_1 (D, A, B);
  and and_1 (C, not_1_out, B);
endmodule

module fullSubtractor (
  input  A,
  input  B,
  input  Bin,
  output D,
  output Bout
);

  wire and_1_out, and_2_out, not_1_out, xnor_1_out;

  xor xor_1 (D, A, B, Bin);
  xnor xnor_1 (xnor_1_out, A, B);
  not not_1 (not_1_out, A);
  and and_1 (and_1_out, not_1_out, B);
  and and_2 (and_2_out, xnor_1_out, Bin);
  or or_1 (Bout, and_2_out, and_1_out);
endmodule
